# Fritzing sketch Schematic (saved by Fritzing 0.9.3b)
breadboards: 1

parts:
  Raspberry_Pi_Zero1 = Raspberry Pi Zero
  DS1 = DS18B20 1-Wire Temperature Sensor [part_number=DS18B20]
  Part1 = Barometric Pressure Sensor - BMP180 Breakout (GY-68)
  RHT1 = Humidity and Temperature Sensor RHT03
  DS2 = DS18B20 1-Wire Temperature Sensor [part_number=DS18B20]

nets:
  3V3: Raspberry_Pi_Zero1.3v3, Raspberry_Pi_Zero1.3V3, DS1.VDD, DS2.VDD
  N1: Raspberry_Pi_Zero1.GPIO2, Part1.SDA
  N2: Raspberry_Pi_Zero1.GPIO3, Part1.SCL
  N3: Raspberry_Pi_Zero1.GPIO4, DS1.DQ, DS2.DQ
  N4: Raspberry_Pi_Zero1.GPIO11, RHT1.Data-signal
  GND: Raspberry_Pi_Zero1.GND, DS1.GND, RHT1.GND_2, DS2.GND
  VCC: Raspberry_Pi_Zero1.5V, Part1.VCC, RHT1.Vcc
  N5: Part1.GND, RHT1.GND_1
